# Fritzing sketch ParkDistance (saved by Fritzing 0.9.3b)
circuit board: 11.4653cm x 5.60916cm
breadboards: 1

parts:
  J1 = female pin header, 8 pins [form="♀ (female)"]
  J2 = female pin header, 8 pins [form="♀ (female)"]
  MAX7219 = STP16CP05 [package=so-24dw]
  10k = Resistor [tolerance=±5% resistance=10k package="0805 [SMD]"]
  X1 = USB Connectors [package=usb-minib-nostop]
  C1 = Tantalum Capacitor [capacitance=1µF package="B 3528 [SMD, tantalum]"]
  J7 = female pin header, 8 pins [form="♀ (female)"]
  J8 = female pin header, 8 pins [form="♀ (female)"]
  C2 = Tantalum Capacitor [capacitance=1µF package="B 3528 [SMD, tantalum]"]
  10k_2 = Resistor [tolerance=±5% resistance=10k package="0805 [SMD]"]
  MAX7220 = STP16CP05 [package=so-24dw]
  J9 = female pin header, 8 pins [form="♀ (female)"]
  J10 = female pin header, 8 pins [form="♀ (female)"]
  C3 = Tantalum Capacitor [capacitance=1µF package="B 3528 [SMD, tantalum]"]
  10k_3 = Resistor [tolerance=±5% resistance=10k package="0805 [SMD]"]
  MAX7221 = STP16CP05 [package=so-24dw]

nets:
  N1: J1.pin1, MAX7219.SDO
  N2: J1.pin2, MAX7219.OUT9
  N3: J1.pin3, MAX7219.OUT0
  N4: J1.pin4, MAX7219.OUT12
  N5: J1.pin5, MAX7219.CLK
  N6: J1.pin6, MAX7219.OUT11
  N7: J1.pin7, MAX7219.REXT
  N8: J1.pin8, MAX7219.OUT3
  N9: J2.pin1, MAX7219.OUT2
  N10: J2.pin2, MAX7219.OUT6
  N11: J2.pin3, MAX7219.OUT10
  N12: J2.pin4, MAX7219.~OE
  N13: J2.pin5, MAX7219.SDI
  N14: J2.pin6, MAX7219.OUT15
  N15: J2.pin7, MAX7219.OUT1
  N16: J2.pin8, MAX7219.OUT5
  N17: MAX7219.LE, MAX7219.OUT4, X1.GND, C1.-
  N18: MAX7219.OUT13, 10k.Pin_0
  N19: MAX7219.OUT14, 10k.Pin_1, X1.VBUS, C1.+
  N20: J7.pin1, MAX7220.OUT2
  N21: J7.pin2, MAX7220.OUT6
  N22: J7.pin3, MAX7220.OUT10
  N23: J7.pin4, MAX7220.~OE
  N24: J7.pin5, MAX7220.SDI
  N25: J7.pin6, MAX7220.OUT15
  N26: J7.pin7, MAX7220.OUT1
  N27: J7.pin8, MAX7220.OUT5
  N28: J8.pin1, MAX7220.SDO
  N29: J8.pin2, MAX7220.OUT9
  N30: J8.pin3, MAX7220.OUT0
  N31: J8.pin4, MAX7220.OUT12
  N32: J8.pin5, MAX7220.CLK
  N33: J8.pin6, MAX7220.OUT11
  N34: J8.pin7, MAX7220.REXT
  N35: J8.pin8, MAX7220.OUT3
  N36: C2.-, MAX7220.LE, MAX7220.OUT4
  N37: C2.+, 10k_2.Pin_1, MAX7220.OUT14
  N38: 10k_2.Pin_0, MAX7220.OUT13
  N39: J9.pin1, MAX7221.OUT2
  N40: J9.pin2, MAX7221.OUT6
  N41: J9.pin3, MAX7221.OUT10
  N42: J9.pin4, MAX7221.~OE
  N43: J9.pin5, MAX7221.SDI
  N44: J9.pin6, MAX7221.OUT15
  N45: J9.pin7, MAX7221.OUT1
  N46: J9.pin8, MAX7221.OUT5
  N47: J10.pin1, MAX7221.SDO
  N48: J10.pin2, MAX7221.OUT9
  N49: J10.pin3, MAX7221.OUT0
  N50: J10.pin4, MAX7221.OUT12
  N51: J10.pin5, MAX7221.CLK
  N52: J10.pin6, MAX7221.OUT11
  N53: J10.pin7, MAX7221.REXT
  N54: J10.pin8, MAX7221.OUT3
  N55: C3.-, MAX7221.LE, MAX7221.OUT4
  N56: C3.+, 10k_3.Pin_1, MAX7221.OUT14
  N57: 10k_3.Pin_0, MAX7221.OUT13
